# Fritzing sketch MecaGlove Structure (saved by Fritzing 0.9.3b)

parts:
  Part1 = SparkFun Motor Driver TB6612FNG (v11) [part_number=ROB-14451]
  Part2 = SparkFun Motor Driver TB6612FNG (v11) [part_number=ROB-14451]
  M1 = DC Motor
  M2 = DC Motor
  M3 = DC Motor
  M4 = DC Motor
  C1 = Electrolytic Capacitor [capacitance=1µF package="100 mil [THT, electrolytic]"]
  Part4 = NRF24L01
  VCC2 = Battery  # not connected
  VCC3 = Battery
  Part6 = Arduino Mega 2560 (Rev3)
  A1 = Esp32-c3 super mini
  J1 = Piezo Speaker
  LED1 = LED - 3mm [color="Red (633nm)" package="3 mm [THT]"]
  Part7 = InvenSense MPU6050
  C2 = Electrolytic Capacitor [capacitance=1µF package="100 mil [THT, electrolytic]"]
  Part8 = NRF24L01
  S1 = SWITCH-MOMENTARY-2 [package=tactile_switch_tall]
  S2 = SWITCH-MOMENTARY-2 [package=tactile_switch_tall]
  Bat1 = battery_holder_single_18650
  A2 = HC-SR04 Ultrasonic Distance Sensor
  U1 = Mini-360 DC-DC Buck converter [package=THT]
  U2 = SWITCH_SPDT [package=kps-1290]  # not connected
  OLED_I2C1 = OLED 128x64 I2C Monochrome Display

nets:
  N1: Part1.B01, M1.pin_1
  N2: Part1.B02, M1.pin_2
  N3: Part1.A02, M4.pin_1
  N4: Part1.A01, M4.pin_2
  GND: Part1.GND, Part2.GND, C1.-, Part4.GND, Part6.GND, J1.pin1, LED1.cathode, A2.GND
  VCC: Part1.VCC, Part1.STBY, Part2.VCC, Part2.STBY, Part6.5V, A2.VCC
  N5: Part1.VM, Part2.VM, VCC3.+, U1.IN+
  N6: Part1.PWMA, Part6.D2_PWM
  N7: Part1.AIN2, Part6.D23
  N8: Part1.AIN1, Part6.D22
  N9: Part1.BIN1, Part6.D24
  N10: Part1.BIN2, Part6.D25
  N11: Part1.PWMB, Part6.D3_PWM
  N12: Part2.B01, M2.pin_1
  N13: Part2.B02, M2.pin_2
  N14: Part2.A02, M3.pin_1
  N15: Part2.A01, M3.pin_2
  N16: Part2.PWMA, Part6.D4_PWM
  N17: Part2.AIN2, Part6.D27
  N18: Part2.AIN1, Part6.D26
  N19: Part2.BIN1, Part6.D28
  N20: Part2.BIN2, Part6.D29
  N21: Part2.PWMB, Part6.D5_PWM
  VCC_2: C1.+, Part4.VCC, Part6.3V3
  N22: Part4.MOSI, Part6.D51
  N23: Part4.CSN, Part6.D49
  N24: Part4.MISO, Part6.D50
  N25: Part4.SCK, Part6.D52
  N26: Part4.CE, Part6.D48
  N27: VCC3.-, U1.IN-
  N28: Part6.D13_PWM, LED1.anode
  N29: Part6.D12_PWM, J1.pin2
  N30: A1.Pin_1, Part8.MISO
  N31: A1.Pin_2, Part8.SCK
  N32: A1.Pin_3, Part8.CSN
  N33: A1.Pin_4, Part7.SDA, OLED_I2C1.SDA
  N34: A1.Pin_5, Part7.SCL, OLED_I2C1.SCK
  N35: A1.Pin_9, S1.2
  N36: A1.Pin_10, S2.1
  N37: A1.Pin_12, Part8.CE
  N38: A1.Pin_13, Part8.MOSI
  VCC_3: A1.Pin_14, Part7.VCC, C2.+, Part8.VCC, OLED_I2C1.VDD
  GND_2: A1.Pin_15, Part7.GND, C2.-, Part8.GND, S1.1, S2.2, Bat1.+#0, OLED_I2C1.GND
  N39: A1.Pin_16, Bat1.+#1

custom parts:
  SparkFun Motor Driver TB6612FNG (v11): The TB6612FNG Motor Driver can control up to two DC motors at a constant current of 1.2A (3.2A peak). Two input signals (IN1 and IN2) can be used to control the motor in one of four function modes: CW, CCW, short-brake and stop. The two motor outputs (A and B) can be separately controlled, and the speed of each motor is controlled via a PWM input signal with a frequency up to 100kHz. The STBY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
  Battery: Your standard 2x 18650 battery pack (7,4 Volts)
  Esp32-c3 super mini: ESP32-C3 Development Board ESP32 SuperMini Development Board ESP32 Development Board WiFi Bluetooth.
  battery_holder_single_18650: single 18650 battery holder
  HC-SR04 Ultrasonic Distance Sensor: The HC-SR04 is an ultrasonic distance sensor. It is capable of providing measurement for ranges of 2cm to 400cm. The module operates at 5V.
  Mini-360 DC-DC Buck converter: Mini-360 DC-DC Buck converter. Tiny buck step down voltage converter, input voltage 4.75 to 23V output 1 to 17V adjustable. Available from ebay and the like.
